// Logisim project 2to4Decoder.circ as structural Verilog: 1 circuit, main circuit main
module main (
  input  A0,
  input  A1,
  output D0,
  output D1,
  output D2,
  output D3
);

  wire not_1_out, not_2_out;

  not not_1 (not_1_out, A0);
  not not_2 (not_2_out, A1);
  and and_1 (D0, not_1_out, not_2_out);
  and and_2 (D1, A0, not_2_out);
  and and_3 (D2, not_1_out, A1);
  and and_4 (D3, A0, A1);

  // Notes on the sheet:
  //   2 to 4 Decoder
endmodule
