// Logisim project Full_Adder.circ as structural Verilog: 2 circuits, main circuit main
module main (
  input  Cin,
  input  A,
  input  B,
  output S,
  output Cout
);

  wire and_1_out, and_2_out, xor_1_out;

  xor xor_1 (xor_1_out, A, B);
  and and_1 (and_1_out, A, B);
  xor xor_2 (S, xor_1_out, Cin);
  and and_2 (and_2_out, Cin, xor_1_out);
  or or_1 (Cout, and_2_out, and_1_out);

  // Notes on the sheet:
  //   Full ADDER
endmodule

module FourBit (
  input  A3,
  input  B3,
  input  A2,
  input  B2,
  input  A1,
  input  B1,
  input  A0,
  input  B0,
  input  Cin0,
  output out_10,
  output S3,
  output S2,
  output S1,
  output S0
);

  wire main_2_cout, main_3_cout, main_4_cout;

  main main_1 (.A(A3), .B(B3), .Cin(main_2_cout), .S(S3), .Cout(out_10));
  main main_2 (.A(A2), .B(B2), .Cin(main_3_cout), .S(S2), .Cout(main_2_cout));
  main main_3 (.A(A1), .B(B1), .Cin(main_4_cout), .S(S1), .Cout(main_3_cout));
  main main_4 (.A(A0), .B(B0), .Cin(Cin0), .S(S0), .Cout(main_4_cout));

  // Notes on the sheet:
  //   Cout
  //   Cin3
  //   Cin2
  //   Cin1
endmodule
