// Logisim project NAND_NMOS.circ as structural Verilog: 1 circuit, main circuit main
module main (
  input  A,
  input  B,
  output C
);

  wire transistor_2_out;

  Pull_Resistor #(.pull(1)) pull_resistor_1 (.node(C));
  Transistor #(.\type ("n")) transistor_1 (.in(transistor_2_out), .out(C), .gate(A));
  Transistor #(.\type ("n")) transistor_2 (.in(1'b0), .out(transistor_2_out), .gate(B));

  // Notes on the sheet:
  //   NAND with NMOS
endmodule
