// Logisim project NOR_NMOS.circ as structural Verilog: 1 circuit, main circuit main
module main (
  input  A,
  input  B,
  output C
);

  Transistor #(.\type ("n")) transistor_1 (.in(1'b0), .out(C), .gate(A));
  Pull_Resistor #(.pull(1)) pull_resistor_1 (.node(C));
  Transistor #(.\type ("n")) transistor_2 (.in(1'b0), .out(C), .gate(B));

  // Notes on the sheet:
  //   NOR with NMOS
endmodule
