// Logisim project NOT_NMOS.circ as structural Verilog: 1 circuit, main circuit main
module main (
  input  A,
  output Anot
);

  Pull_Resistor #(.pull(1)) pull_resistor_1 (.node(Anot));
  Transistor #(.\type ("n")) transistor_1 (.in(1'b0), .out(Anot), .gate(A));

  // Notes on the sheet:
  //   NOT with NMOS
endmodule
