// Logisim project Register_Set_Library -2003027.circ as structural Verilog: 5 circuits, main circuit L_1_bit_Register_511be1f4
module L_1_bit_Register_511be1f4 (
  input  Din,
  input  Sel,
  input  Clock,
  output Dout
);

  wire l_1_bit_2to1_mux_76676022_1_out;

  L_1_bit_2to1_MUX_76676022 l_1_bit_2to1_mux_76676022_1 (
    .A(Dout), .Sel(Sel), .B(Din), .Out(l_1_bit_2to1_mux_76676022_1_out));
  D_Flip_Flop d_ff_1 (.D(l_1_bit_2to1_mux_76676022_1_out), .clk(Clock), .Q(Dout));  // open: Qn, preset, reset
endmodule

module L_1_bit_2to1_MUX_76676022 (
  input  A,
  input  Sel,
  input  B,
  output Out
);

  wire and_1_out, and_2_out, not_1_out;

  not not_1 (not_1_out, Sel);
  and and_1 (and_1_out, A, not_1_out);
  and and_2 (and_2_out, Sel, B);
  or or_1 (Out, and_1_out, and_2_out);
endmodule

module L_8_bit_Register_cb06da42 (
  input  [7:0] Din_7_0_d79f9437,
  input  Sel,
  input  Clock,
  output [7:0] Dout_7_0_4d2bfa11
);

  L_1_bit_Register_511be1f4 l_1_bit_register_511be1f4_1 (
    .Din(Din_7_0_d79f9437[7]), .Sel(Sel), .Clock(Clock), .Dout(Dout_7_0_4d2bfa11[7]));
  L_1_bit_Register_511be1f4 l_1_bit_register_511be1f4_2 (
    .Din(Din_7_0_d79f9437[6]), .Sel(Sel), .Clock(Clock), .Dout(Dout_7_0_4d2bfa11[6]));
  L_1_bit_Register_511be1f4 l_1_bit_register_511be1f4_3 (
    .Din(Din_7_0_d79f9437[5]), .Sel(Sel), .Clock(Clock), .Dout(Dout_7_0_4d2bfa11[5]));
  L_1_bit_Register_511be1f4 l_1_bit_register_511be1f4_4 (
    .Din(Din_7_0_d79f9437[4]), .Sel(Sel), .Clock(Clock), .Dout(Dout_7_0_4d2bfa11[4]));
  L_1_bit_Register_511be1f4 l_1_bit_register_511be1f4_5 (
    .Din(Din_7_0_d79f9437[3]), .Sel(Sel), .Clock(Clock), .Dout(Dout_7_0_4d2bfa11[3]));
  L_1_bit_Register_511be1f4 l_1_bit_register_511be1f4_6 (
    .Din(Din_7_0_d79f9437[2]), .Sel(Sel), .Clock(Clock), .Dout(Dout_7_0_4d2bfa11[2]));
  L_1_bit_Register_511be1f4 l_1_bit_register_511be1f4_7 (
    .Din(Din_7_0_d79f9437[1]), .Sel(Sel), .Clock(Clock), .Dout(Dout_7_0_4d2bfa11[1]));
  L_1_bit_Register_511be1f4 l_1_bit_register_511be1f4_8 (
    .Din(Din_7_0_d79f9437[0]), .Sel(Sel), .Clock(Clock), .Dout(Dout_7_0_4d2bfa11[0]));
endmodule

module fourbitregister (
  input  in_1,
  input  in_2,
  input  in_3,
  input  in_4,
  input  SEL,
  output [3:0] out_6
);

  wire CLK_out;

  Clock CLK (.out(CLK_out));
  L_1_bit_Register_511be1f4 l_1_bit_register_511be1f4_1 (.Din(in_1), .Sel(SEL), .Clock(CLK_out), .Dout(out_6[3]));
  L_1_bit_Register_511be1f4 l_1_bit_register_511be1f4_2 (.Din(in_2), .Sel(SEL), .Clock(CLK_out), .Dout(out_6[2]));
  L_1_bit_Register_511be1f4 l_1_bit_register_511be1f4_3 (.Din(in_3), .Sel(SEL), .Clock(CLK_out), .Dout(out_6[1]));
  L_1_bit_Register_511be1f4 l_1_bit_register_511be1f4_4 (.Din(in_4), .Sel(SEL), .Clock(CLK_out), .Dout(out_6[0]));
endmodule

module flagregister (
  input  CF1,
  input  SF1,
  input  ZF1,
  output CF2,
  output SF2,
  output ZF2
);

  wire CLK_out;

  Clock CLK (.out(CLK_out));
  L_1_bit_Register_511be1f4 l_1_bit_register_511be1f4_1 (.Din(CF1), .Sel(1'b1), .Clock(CLK_out), .Dout(CF2));
  L_1_bit_Register_511be1f4 l_1_bit_register_511be1f4_2 (.Din(SF1), .Sel(1'b1), .Clock(CLK_out), .Dout(SF2));
  L_1_bit_Register_511be1f4 l_1_bit_register_511be1f4_3 (.Din(ZF1), .Sel(1'b1), .Clock(CLK_out), .Dout(ZF2));
endmodule
